// Digital circuit RPS_AIV2.dig as structural Verilog
module RPS_AIV2 (
  input  clk,
  input  in_2,
  input  in_3,
  input  in_4,
  input  in_5,
  input  in_6,
  input  in_7,
  input  in_8,
  input  in_9,
  input  in_10,
  input  in_11,
  input  in_12,
  input  in_13,
  input  in_14,
  input  in_15,
  input  in_16,
  input  in_17,
  input  in_18,
  input  clk_2,
  input  clk_3,
  input  in_21
);

  wire _7448_1_p10, _7448_1_p11, _7448_1_p12, _7448_1_p13, _7448_1_p14, _7448_1_p15, _7448_1_p16,
       _7448_2_p10, _7448_2_p11, _7448_2_p12, _7448_2_p13, _7448_2_p14, _7448_2_p15, _7448_2_p16,
       _7448_3_p10, _7448_3_p11, _7448_3_p12, _7448_3_p13, _7448_3_p14, _7448_3_p15, _7448_3_p16,
       _7448_4_p10, _7448_4_p11, _7448_4_p12, _7448_4_p13, _7448_4_p14, _7448_4_p15, _7448_4_p16,
       _7448_5_p10, _7448_5_p11, _7448_5_p12, _7448_5_p13, _7448_5_p14, _7448_5_p15, _7448_5_p16,
       _7448_6_p10, _7448_6_p11, _7448_6_p12, _7448_6_p13, _7448_6_p14, _7448_6_p15, _7448_6_p16,
       _74138_1_p4, _74138_1_p9, _74138_1_p10, _74138_1_p11, _74138_1_p12, _74138_1_p13, _74138_1_p14,
       _74138_1_p15, _74138_1_p16, _74139_1_p9, _74139_1_p10, _74139_1_p11, _74139_1_p12, _74164_1_p7,
       _74164_1_p8, _74164_2_p7, _74164_2_p8, _74164_3_p7, _74164_3_p8, _74193_1_p7, _74193_1_p11,
       _74193_1_p12, _74193_1_p13, _74193_2_p11, _74193_2_p12, _74193_2_p13, _74193_2_p14, _74193_3_p11,
       _74193_3_p12, _74193_3_p13, _74193_3_p14, _74193_4_p11, _74193_4_p12, _74193_4_p13, _74193_4_p14,
       _74193_5_p11, _74193_5_p12, _74193_5_p13, _74193_5_p14, _74193_6_p11, _74193_6_p12, _74193_6_p13,
       _74193_6_p14, _74193_7_p11, _74193_7_p12, _74193_7_p13, _74193_7_p14, _74193_8_p7, _74193_8_p11,
       _74193_9_p7, _74193_9_p11, _74193_10_p7, _74193_10_p11, _74373_1_p13, _74373_1_p14, _74373_1_p15,
       _74373_1_p16, _74373_1_p17, _74373_1_p18, _74373_1_p19, _74373_1_p20, _74373_2_p14, _74373_2_p15,
       _74373_2_p16, _74373_2_p17, _74373_2_p18, _74373_2_p19, _74373_2_p20, _74373_2_p21, _744017_1_p1,
       _744017_1_p3, _744017_1_p6, _744017_1_p7, _744017_1_p8, _744017_1_p9, _744017_1_p10, _744017_1_p11,
       _744017_1_p12, _744017_1_p13, _744017_2_p5, _744017_2_p6, _744017_2_p7, _744017_2_p8, _744017_2_p10,
       _744017_2_p11, _744017_2_p12, and_1_out, and_2_out, and_3_out, and_4_out, and_5_out, and_6_out,
       and_7_out, and_8_out, and_9_out, and_10_out, button_1_out, button_2_out, button_3_out, button_4_out,
       driver_1_out, driver_4_out, driver_24_out, driver_25_out, driver_33_out, driver_44_out, driver_45_out,
       driver_46_out, driver_47_out, driverinvsel_2_out, driverinvsel_20_out, driverinvsel_21_out,
       driverinvsel_22_out, not_1_out, not_2_out, not_3_out, not_4_out, not_5_out, not_6_out, not_7_out,
       not_8_out, not_9_out, not_11_out, not_12_out, not_13_out, not_14_out, not_15_out, not_16_out,
       not_17_out, not_18_out, rom_1_d, rps_module_1_lose, rps_module_1_tie, rps_module_1_win, xor_1_out,
       xor_2_out, xor_3_out, xor_4_out, xor_5_out, xor_6_out;
  wire [15:0] counter_1_out, driver_18_out, driver_23_out;

  // _744017 _744017_1: pin names not known; wires that end beside it: _744017_1_p1, clk, _744017_1_p3, 1'b1, 1'b0, _744017_1_p6, _744017_1_p7, _744017_1_p8, _744017_1_p9, _744017_1_p10, _744017_1_p11, _744017_1_p12, _744017_1_p13, _744017_1_p3
  assign driver_1_out = and_4_out ? 1'b1 : 1'bz;  // Driver driver_1
  assign driver_1_out = and_2_out ? 1'b0 : 1'bz;  // Driver driver_2
  assign driver_1_out = and_3_out ? 1'b1 : 1'bz;  // Driver driver_3
  PullDown pulldown_1 (.out(driver_1_out));
  assign driver_4_out = and_4_out ? 1'b0 : 1'bz;  // Driver driver_4
  assign driver_4_out = and_2_out ? 1'b1 : 1'bz;  // Driver driver_5
  assign driver_4_out = and_3_out ? 1'b1 : 1'bz;  // Driver driver_6
  PullDown pulldown_2 (.out(driver_4_out));
  or or_1 (_744017_1_p1, and_4_out, and_2_out, and_3_out);
  assign driver_18_out[0] = _744017_1_p6 ? driver_1_out : 1'bz;  // Driver driver_7
  assign driver_18_out[1] = _744017_1_p6 ? driver_4_out : 1'bz;  // Driver driver_8
  assign driver_18_out[2] = _744017_1_p7 ? driver_1_out : 1'bz;  // Driver driver_9
  assign driver_18_out[3] = _744017_1_p7 ? driver_4_out : 1'bz;  // Driver driver_10
  assign driver_18_out[4] = _744017_1_p8 ? driver_1_out : 1'bz;  // Driver driver_11
  assign driver_18_out[5] = _744017_1_p8 ? driver_4_out : 1'bz;  // Driver driver_12
  assign driver_18_out[6] = _744017_1_p9 ? driver_1_out : 1'bz;  // Driver driver_13
  assign driver_18_out[7] = _744017_1_p9 ? driver_4_out : 1'bz;  // Driver driver_14
  assign driver_18_out[8] = _744017_1_p10 ? driver_1_out : 1'bz;  // Driver driver_15
  assign driver_18_out[9] = _744017_1_p10 ? driver_4_out : 1'bz;  // Driver driver_16
  assign driver_18_out[10] = _744017_1_p11 ? driver_1_out : 1'bz;  // Driver driver_17
  assign driver_18_out[11] = _744017_1_p11 ? driver_4_out : 1'bz;  // Driver driver_18
  assign driver_18_out[12] = _744017_1_p12 ? driver_1_out : 1'bz;  // Driver driver_19
  assign driver_18_out[13] = _744017_1_p12 ? driver_4_out : 1'bz;  // Driver driver_20
  assign driver_18_out[14] = _744017_1_p13 ? driver_1_out : 1'bz;  // Driver driver_21
  assign driver_18_out[15] = _744017_1_p13 ? driver_4_out : 1'bz;  // Driver driver_22
  PullDown pulldown_3 (.out(driver_18_out[15]));
  PullDown pulldown_4 (.out(driver_18_out[14]));
  PullDown pulldown_5 (.out(driver_18_out[10]));
  PullDown pulldown_6 (.out(driver_18_out[11]));
  PullDown pulldown_7 (.out(driver_18_out[7]));
  PullDown pulldown_8 (.out(driver_18_out[6]));
  PullDown pulldown_9 (.out(driver_18_out[5]));
  PullDown pulldown_10 (.out(driver_18_out[4]));
  PullDown pulldown_11 (.out(driver_18_out[8]));
  PullDown pulldown_12 (.out(driver_18_out[9]));
  PullDown pulldown_13 (.out(driver_18_out[13]));
  PullDown pulldown_14 (.out(driver_18_out[12]));
  PullDown pulldown_15 (.out(driver_18_out[3]));
  PullDown pulldown_16 (.out(driver_18_out[2]));
  PullDown pulldown_17 (.out(driver_18_out[1]));
  PullDown pulldown_18 (.out(driver_18_out[0]));
  assign driver_23_out = in_18 ? {in_17, in_15, in_13, in_11, in_9, in_7, in_5, in_3, in_16, in_14, in_12, in_10, in_8, in_6, in_4, in_2} : 16'bz;  // Driver driver_23
  assign driver_23_out = ~in_18 ? driver_18_out : 16'bz;  // DriverInvSel driverinvsel_1
  PullDown #(.Bits(16)) pulldown_19 (.out(driver_23_out));
  assign driverinvsel_2_out = ~_74138_1_p4 ? clk : 1'bz;  // DriverInvSel driverinvsel_2
  PullDown pulldown_20 (.out(driverinvsel_2_out));
  // _74193 _74193_1: pin names not known; wires that end beside it: 1'b1, driverinvsel_2_out, 1'b0, 1'b0, 1'b0, 1'b0, _74193_1_p7, 1'b1, 1'b1, 1'b0, _74193_1_p11, _74193_1_p12, _74193_1_p13, _74193_1_p7
  assign driver_18_out[15] = ~_744017_1_p13 ? _74373_2_p21 : 1'bz;  // DriverInvSel driverinvsel_3
  assign driver_18_out[14] = ~_744017_1_p13 ? _74373_1_p20 : 1'bz;  // DriverInvSel driverinvsel_4
  assign driver_18_out[13] = ~_744017_1_p12 ? _74373_2_p20 : 1'bz;  // DriverInvSel driverinvsel_5
  assign driver_18_out[12] = ~_744017_1_p12 ? _74373_1_p19 : 1'bz;  // DriverInvSel driverinvsel_6
  assign driver_18_out[11] = ~_744017_1_p11 ? _74373_2_p19 : 1'bz;  // DriverInvSel driverinvsel_7
  assign driver_18_out[10] = ~_744017_1_p11 ? _74373_1_p18 : 1'bz;  // DriverInvSel driverinvsel_8
  assign driver_18_out[9] = ~_744017_1_p10 ? _74373_2_p18 : 1'bz;  // DriverInvSel driverinvsel_9
  assign driver_18_out[8] = ~_744017_1_p10 ? _74373_1_p17 : 1'bz;  // DriverInvSel driverinvsel_10
  assign driver_18_out[7] = ~_744017_1_p9 ? _74373_2_p17 : 1'bz;  // DriverInvSel driverinvsel_11
  assign driver_18_out[6] = ~_744017_1_p9 ? _74373_1_p16 : 1'bz;  // DriverInvSel driverinvsel_12
  assign driver_18_out[5] = ~_744017_1_p8 ? _74373_2_p16 : 1'bz;  // DriverInvSel driverinvsel_13
  assign driver_18_out[4] = ~_744017_1_p8 ? _74373_1_p15 : 1'bz;  // DriverInvSel driverinvsel_14
  assign driver_18_out[3] = ~_744017_1_p7 ? _74373_2_p15 : 1'bz;  // DriverInvSel driverinvsel_15
  assign driver_18_out[2] = ~_744017_1_p7 ? _74373_1_p14 : 1'bz;  // DriverInvSel driverinvsel_16
  assign driver_18_out[1] = ~_744017_1_p6 ? _74373_2_p14 : 1'bz;  // DriverInvSel driverinvsel_17
  assign driver_18_out[0] = ~_744017_1_p6 ? _74373_1_p13 : 1'bz;  // DriverInvSel driverinvsel_18
  assign driver_24_out = in_18 ? in_18 : 1'bz;  // Driver driver_24
  // _74138 _74138_1: pin names not known; wires that end beside it: _74193_1_p11, _74193_1_p12, _74193_1_p13, _74138_1_p4, 1'b0, 1'b0, 1'b1, 1'b0, _74138_1_p9, _74138_1_p10, _74138_1_p11, _74138_1_p12, _74138_1_p13, _74138_1_p14, _74138_1_p15, _74138_1_p16
  assign driver_24_out = ~in_18 ? _744017_1_p1 : 1'bz;  // DriverInvSel driverinvsel_19
  // _74373 _74373_1: pin names not known; wires that end beside it: 1'b0, driver_24_out, driver_23_out[0], driver_23_out[2], driver_23_out[4], driver_23_out[6], driver_23_out[8], driver_23_out[10], driver_23_out[12], driver_23_out[14], 1'b1, 1'b0, _74373_1_p13, _74373_1_p14, _74373_1_p15, _74373_1_p16, _74373_1_p17, _74373_1_p18, _74373_1_p19, _74373_1_p20
  // _74373 _74373_2: pin names not known; wires that end beside it: 1'b0, driver_24_out, driver_23_out[1], driver_23_out[3], driver_23_out[5], driver_23_out[7], driver_23_out[9], driver_23_out[11], driver_23_out[13], driver_23_out[15], 1'b1, 1'b0, _74138_1_p4, _74373_2_p14, _74373_2_p15, _74373_2_p16, _74373_2_p17, _74373_2_p18, _74373_2_p19, _74373_2_p20, _74373_2_p21
  not not_1 (not_1_out, _74138_1_p9);
  not not_2 (not_2_out, _74138_1_p10);
  not not_3 (not_3_out, _74138_1_p11);
  not not_4 (not_4_out, _74138_1_p12);
  not not_5 (not_5_out, _74138_1_p13);
  not not_6 (not_6_out, _74138_1_p14);
  not not_7 (not_7_out, _74138_1_p15);
  not not_8 (not_8_out, _74138_1_p16);
  and and_1 (and_1_out, clk_2, rom_1_d);
  assign driver_25_out = not_1_out ? _74373_1_p13 : 1'bz;  // Driver driver_25
  assign driver_25_out = not_2_out ? _74373_1_p14 : 1'bz;  // Driver driver_26
  assign driver_25_out = not_3_out ? _74373_1_p15 : 1'bz;  // Driver driver_27
  assign driver_25_out = not_4_out ? _74373_1_p16 : 1'bz;  // Driver driver_28
  assign driver_25_out = not_5_out ? _74373_1_p17 : 1'bz;  // Driver driver_29
  assign driver_25_out = not_6_out ? _74373_1_p18 : 1'bz;  // Driver driver_30
  assign driver_25_out = not_7_out ? _74373_1_p19 : 1'bz;  // Driver driver_31
  assign driver_25_out = not_8_out ? _74373_1_p20 : 1'bz;  // Driver driver_32
  assign driver_33_out = not_1_out ? _74373_2_p14 : 1'bz;  // Driver driver_33
  assign driver_33_out = not_2_out ? _74373_2_p15 : 1'bz;  // Driver driver_34
  assign driver_33_out = not_3_out ? _74373_2_p16 : 1'bz;  // Driver driver_35
  assign driver_33_out = not_4_out ? _74373_2_p17 : 1'bz;  // Driver driver_36
  assign driver_33_out = not_5_out ? _74373_2_p18 : 1'bz;  // Driver driver_37
  assign driver_33_out = not_6_out ? _74373_2_p19 : 1'bz;  // Driver driver_38
  assign driver_33_out = not_7_out ? _74373_2_p20 : 1'bz;  // Driver driver_39
  assign driver_33_out = not_8_out ? _74373_2_p21 : 1'bz;  // Driver driver_40
  // _744017 _744017_2: pin names not known; wires that end beside it: 1'b1, 1'b0, 1'b0, and_1_out, _744017_2_p5, _744017_2_p6, _744017_2_p7, _744017_2_p8, _744017_2_p5, _744017_2_p10, _744017_2_p11, _744017_2_p12
  not not_9 (not_9_out, rom_1_d);
  PullDown pulldown_21 (.out(driver_25_out));
  PullDown pulldown_22 (.out(driver_33_out));
  assign _744017_2_p10 = not_9_out ? _744017_2_p6 : 1'bz;  // Driver driver_41
  assign _744017_2_p11 = not_9_out ? _744017_2_p7 : 1'bz;  // Driver driver_42
  assign _744017_2_p12 = not_9_out ? _744017_2_p8 : 1'bz;  // Driver driver_43
  // _74139 _74139_1: pin names not known; wires that end beside it: driver_25_out, driver_33_out, 1'b0, 1'b1, 1'b1, 1'b1, 1'b1, 1'b0, _74139_1_p9, _74139_1_p10, _74139_1_p11, _74139_1_p12
  PullDown pulldown_23 (.out(_744017_2_p10));
  PullDown pulldown_24 (.out(_744017_2_p11));
  PullDown pulldown_25 (.out(_744017_2_p12));
  // Not not_10 has open pins: in=_74139_1_p9, out=open
  not not_11 (not_11_out, _74139_1_p10);
  not not_12 (not_12_out, _74139_1_p11);
  not not_13 (not_13_out, _74139_1_p12);
  Button button_1 (.out(button_1_out));
  Button button_2 (.out(button_2_out));
  Button button_3 (.out(button_3_out));
  Button button_4 (.out(button_4_out));
  not not_14 (not_14_out, button_4_out);
  not not_15 (not_15_out, _74138_1_p4);
  RPS_MODULE rps_module_1 (
    .ROCK(button_1_out), .PAPER(button_2_out), .SCISSORS(button_3_out), .AI_ROCK(not_11_out),
    .AI_PAPER(not_12_out), .AI_SCISSOR(not_13_out), .Win(rps_module_1_win), .Tie(rps_module_1_tie),
    .Lose(rps_module_1_lose), .SE(_74138_1_p4));
  not not_16 (not_16_out, and_2_out);
  not not_17 (not_17_out, and_3_out);
  not not_18 (not_18_out, and_4_out);
  // _74164 _74164_1: pin names not known; wires that end beside it: button_1_out, not_15_out, 1'b1, not_16_out, 1'b1, 1'b0, _74164_1_p7, _74164_1_p8
  // _74164 _74164_2: pin names not known; wires that end beside it: button_2_out, 1'b1, not_15_out, not_17_out, 1'b1, 1'b0, _74164_2_p7, _74164_2_p8
  // _74164 _74164_3: pin names not known; wires that end beside it: button_3_out, 1'b1, not_15_out, not_18_out, 1'b1, 1'b0, _74164_3_p7, _74164_3_p8
  xor xor_1 (xor_1_out, not_14_out, and_5_out);
  xor xor_2 (xor_2_out, not_14_out, and_6_out);
  xor xor_3 (xor_3_out, not_14_out, and_7_out);
  and and_2 (and_2_out, _74164_1_p7, _74164_1_p8);
  and and_3 (and_3_out, _74164_2_p7, _74164_2_p8);
  and and_4 (and_4_out, _74164_3_p7, _74164_3_p8);
  LED led_1 (.in(rps_module_1_win));
  LED led_2 (.in(rps_module_1_tie));
  LED led_3 (.in(rps_module_1_lose));
  // _74193 _74193_2: pin names not known; wires that end beside it: 1'b1, rps_module_1_lose, 1'b0, 1'b0, 1'b0, 1'b0, 1'b0, xor_3_out, 1'b1, 1'b0, _74193_2_p11, _74193_2_p12, _74193_2_p13, _74193_2_p14
  // _74193 _74193_3: pin names not known; wires that end beside it: 1'b1, rps_module_1_win, 1'b0, 1'b0, 1'b0, 1'b0, 1'b0, xor_1_out, 1'b1, 1'b0, _74193_3_p11, _74193_3_p12, _74193_3_p13, _74193_3_p14
  // _74193 _74193_4: pin names not known; wires that end beside it: 1'b1, rps_module_1_tie, 1'b0, 1'b0, 1'b0, 1'b0, 1'b0, xor_2_out, 1'b1, 1'b0, _74193_4_p11, _74193_4_p12, _74193_4_p13, _74193_4_p14
  and and_5 (and_5_out, _74193_3_p12, _74193_3_p14);
  and and_6 (and_6_out, _74193_4_p12, _74193_4_p14);
  and and_7 (and_7_out, _74193_2_p12, _74193_2_p14);
  assign driverinvsel_20_out = ~1'b0 ? 1'b0 : 1'bz;  // DriverInvSel driverinvsel_20
  assign driverinvsel_21_out = ~1'b0 ? 1'b0 : 1'bz;  // DriverInvSel driverinvsel_21
  assign driverinvsel_22_out = ~1'b0 ? 1'b0 : 1'bz;  // DriverInvSel driverinvsel_22
  // _74193 _74193_5: pin names not known; wires that end beside it: 1'b1, and_5_out, 1'b0, 1'b0, 1'b0, 1'b0, 1'b0, not_14_out, 1'b1, 1'b0, _74193_5_p11, _74193_5_p12, _74193_5_p13, _74193_5_p14
  // _74193 _74193_6: pin names not known; wires that end beside it: 1'b1, and_7_out, 1'b0, 1'b0, 1'b0, 1'b0, 1'b0, not_14_out, 1'b1, 1'b0, _74193_6_p11, _74193_6_p12, _74193_6_p13, _74193_6_p14
  and and_8 (and_8_out, driverinvsel_21_out, driverinvsel_22_out);
  and and_9 (and_9_out, driverinvsel_20_out, driverinvsel_21_out);
  PullDown pulldown_26 (.out(driverinvsel_20_out));
  PullDown pulldown_27 (.out(driverinvsel_22_out));
  PullDown pulldown_28 (.out(driverinvsel_21_out));
  and and_10 (and_10_out, driverinvsel_20_out, driverinvsel_22_out);
  // _7448 _7448_1: pin names not known; wires that end beside it: 1'b1, 1'b0, _74193_5_p11, _74193_5_p12, _74193_5_p13, _74193_5_p14, 1'b1, 1'b1, 1'b1, _7448_1_p10, _7448_1_p11, _7448_1_p12, _7448_1_p13, _7448_1_p14, _7448_1_p15, _7448_1_p16
  // _74193 _74193_7: pin names not known; wires that end beside it: 1'b1, and_6_out, 1'b0, 1'b0, 1'b0, 1'b0, 1'b0, not_14_out, 1'b1, 1'b0, _74193_7_p11, _74193_7_p12, _74193_7_p13, _74193_7_p14
  // _7448 _7448_2: pin names not known; wires that end beside it: 1'b1, 1'b0, _74193_6_p11, _74193_6_p12, _74193_6_p13, _74193_6_p14, 1'b1, 1'b1, 1'b1, _7448_2_p10, _7448_2_p11, _7448_2_p12, _7448_2_p13, _7448_2_p14, _7448_2_p15, _7448_2_p16
  // _74193 _74193_8: pin names not known; wires that end beside it: 1'b1, and_8_out, 1'b0, 1'b0, 1'b0, 1'b0, _74193_8_p7, 1'b1, 1'b1, 1'b0, _74193_8_p11, _74193_8_p7
  // _74193 _74193_9: pin names not known; wires that end beside it: 1'b1, and_10_out, 1'b0, 1'b0, 1'b0, 1'b0, _74193_9_p7, 1'b1, 1'b1, 1'b0, _74193_9_p11, _74193_9_p7
  // _74193 _74193_10: pin names not known; wires that end beside it: 1'b1, and_9_out, 1'b0, 1'b0, 1'b0, 1'b0, _74193_10_p7, 1'b1, 1'b1, 1'b0, _74193_10_p11, _74193_10_p7
  // _7448 _7448_3: pin names not known; wires that end beside it: 1'b1, 1'b0, _74193_7_p11, _74193_7_p12, _74193_7_p13, _74193_7_p14, 1'b1, 1'b1, 1'b1, _7448_3_p10, _7448_3_p11, _7448_3_p12, _7448_3_p13, _7448_3_p14, _7448_3_p15, _7448_3_p16
  xor xor_4 (xor_4_out, _74193_8_p11, _74193_9_p11);
  xor xor_5 (xor_5_out, _74193_8_p11, _74193_10_p11);
  xor xor_6 (xor_6_out, _74193_9_p11, _74193_10_p11);
  assign driver_44_out = 1'b0 ? xor_4_out : 1'bz;  // Driver driver_44
  assign driver_45_out = 1'b0 ? xor_5_out : 1'bz;  // Driver driver_45
  assign driver_46_out = 1'b0 ? xor_6_out : 1'bz;  // Driver driver_46
  PullDown pulldown_29 (.out(driver_46_out));
  PullDown pulldown_30 (.out(driver_45_out));
  PullDown pulldown_31 (.out(driver_44_out));
  // _7448 _7448_4: pin names not known; wires that end beside it: 1'b1, 1'b0, _74193_3_p11, _74193_3_p12, _74193_3_p13, _74193_3_p14, 1'b1, 1'b1, 1'b1, _7448_4_p10, _7448_4_p11, _7448_4_p12, _7448_4_p13, _7448_4_p14, _7448_4_p15, _7448_4_p16
  // _7448 _7448_5: pin names not known; wires that end beside it: 1'b1, 1'b0, _74193_4_p11, _74193_4_p12, _74193_4_p13, _74193_4_p14, 1'b1, 1'b1, 1'b1, _7448_5_p10, _7448_5_p11, _7448_5_p12, _7448_5_p13, _7448_5_p14, _7448_5_p15, _7448_5_p16
  // _7448 _7448_6: pin names not known; wires that end beside it: 1'b1, 1'b0, _74193_2_p11, _74193_2_p12, _74193_2_p13, _74193_2_p14, 1'b1, 1'b1, 1'b1, _7448_6_p10, _7448_6_p11, _7448_6_p12, _7448_6_p13, _7448_6_p14, _7448_6_p15, _7448_6_p16
  assign driver_47_out = in_21 ? clk_3 : 1'bz;  // Driver driver_47
  Counter #(.Bits(16)) counter_1 (.en(1'b1), .C(driver_47_out), .clr(1'b0), .out(counter_1_out));  // open: ovf
  ROM #(.AddrBits(16)) rom_1 (.A(counter_1_out), .sel(1'b1), .D(rom_1_d));
  Seven_Seg #(.persistTime(16)) seven_seg_1 (
    .a(_7448_1_p10), .b(_7448_1_p11), .c(_7448_1_p12), .d(_7448_1_p13), .e(_7448_1_p14), .f(_7448_1_p15),
    .g(_7448_1_p16), .dp(_7448_1_p16));
  Seven_Seg #(.persistTime(16)) seven_seg_2 (
    .a(_7448_3_p10), .b(_7448_3_p11), .c(_7448_3_p12), .d(_7448_3_p13), .e(_7448_3_p14), .f(_7448_3_p15),
    .g(_7448_3_p16), .dp(_7448_3_p16));
  Seven_Seg #(.persistTime(16)) seven_seg_3 (
    .a(_7448_2_p10), .b(_7448_2_p11), .c(_7448_2_p12), .d(_7448_2_p13), .e(_7448_2_p14), .f(_7448_2_p15),
    .g(_7448_2_p16), .dp(_7448_2_p16));
  Seven_Seg #(.persistTime(16)) seven_seg_4 (
    .a(_7448_4_p10), .b(_7448_4_p11), .c(_7448_4_p12), .d(_7448_4_p13), .e(_7448_4_p14), .f(_7448_4_p15),
    .g(_7448_4_p16), .dp(1'b0));
  Seven_Seg #(.persistTime(16)) seven_seg_5 (
    .a(_7448_5_p10), .b(_7448_5_p11), .c(_7448_5_p12), .d(_7448_5_p13), .e(_7448_5_p14), .f(_7448_5_p15),
    .g(_7448_5_p16), .dp(1'b0));
  Seven_Seg #(.persistTime(16)) seven_seg_6 (
    .a(_7448_6_p10), .b(_7448_6_p11), .c(_7448_6_p12), .d(_7448_6_p13), .e(_7448_6_p14), .f(_7448_6_p15),
    .g(_7448_6_p16), .dp(1'b0));

  // Notes on the sheet:
  //   clk: Hz: 50000
  //   in_2: default 1
  //   in_4: default 1
  //   in_5: default 1
  //   in_7: default 1
  //   in_9: default 1
  //   in_10: default 1
  //   in_12: default 1
  //   in_14: default 1
  //   in_15: default 1
  //   in_17: default 1
  //   clk_2: Hz: 50000
  //   clk_3: Hz: 5000
  //   Test
  //   contents of rom_1 (hex, n*v repeats v):
  //   1,0,0,5*1,0,0,1,0,0,0,1,1,0,1,0,1,9,0,0,1,0,9,0,1,1,1,0,64,7*0
  //   ,1,0,0,0,1,0,0,b,0,0,1,13*0,1,0,1,0,0,1,0,0,1,0,1,1,4*0,1,0,0,0
  //   ,1,8*0,1,7*0,1,0,0,1,0,0,1,8*0,1,9*0,1,0,1,14*0,1,5*0,1,0,0,1
  //   ,9*0,1,0,0,0,1,0,1,4*0,1,0,0,1,1,21*0,1,27*0,1,7*0,1,8*0,1,25*0
  //   ,1,0,1,41*0,1,5*0,1,8*0,1,27*0,1,12*0,1,10*0,1,36*0,1,7*0,1,8*0
  //   ,1,24*0,1,12*0,1,61*0,1,11*0,1,5*0,1,16*0,1,110*0,1,10*0,1,78*0
  //   ,1,25*0,1,67*0,1,10*0,1,7*0,1,76*0,1,10*0,1,12*0,1,110*0,1,13*0
  //   ,1,46*0,1,0,0,1,0,0,0,1,5*0,1,85*0,1,13*0,1,119*0,1,0,0,0,1,5*0
  //   ,1,7*0,1,38*0,1,6*0,1,10*0,1,46*0,1,15*0,1,78*0,1,7*0,1,5*0,1
  //   ,10*0,1,27*0,1,88*0,1,218*0,1,6*0,1
  //   RANDOM GNERATOR
  //   TIE
  //   AI
endmodule
