// Digital circuit RPS_MODULE.dig as structural Verilog
module RPS_MODULE (
  input  ROCK,
  input  PAPER,
  input  SCISSORS,
  input  AI_ROCK,
  input  AI_PAPER,
  input  AI_SCISSOR,
  output Win,
  output Tie,
  output Lose,
  output SE
);

  wire _74373_1_p3, _74373_1_p4, _74373_1_p5, and_1_out, and_2_out, and_3_out, and_4_out, and_5_out,
       and_6_out, and_7_out, and_8_out, and_9_out;

  or or_1 (SE, ROCK, PAPER, SCISSORS);
  // _74373 _74373_1: pin names not known; wires that end beside it: 1'b0, SE, _74373_1_p3, _74373_1_p4, _74373_1_p5, 1'b0, 1'b0, 1'b0, 1'b0, 1'b0, 1'b1, 1'b0, Win, Tie, Lose
  PowerSupply powersupply_1 (.VDD(1'b1), .GND(1'b0));
  and and_1 (and_1_out, AI_PAPER, ROCK);
  and and_2 (and_2_out, AI_SCISSOR, PAPER);
  and and_3 (and_3_out, AI_ROCK, SCISSORS);
  and and_4 (and_4_out, AI_SCISSOR, ROCK);
  and and_5 (and_5_out, AI_ROCK, PAPER);
  and and_6 (and_6_out, AI_PAPER, SCISSORS);
  and and_7 (and_7_out, AI_ROCK, ROCK);
  and and_8 (and_8_out, AI_PAPER, PAPER);
  and and_9 (and_9_out, AI_SCISSOR, SCISSORS);
  or or_2 (_74373_1_p5, and_1_out, and_2_out, and_3_out);
  or or_3 (_74373_1_p3, and_4_out, and_5_out, and_6_out);
  or or_4 (_74373_1_p4, and_7_out, and_8_out, and_9_out);
endmodule
